# Fritzing sketch Button_LED (saved by Fritzing 0.9.3b)
breadboards: 1

parts:
  Raspberry_Pi1 = Raspberry Pi 2
  S1 = Pushbutton [package="[SMD]"]
  LED1 = LED - 5mm [color="Red (633nm)" package="5 mm [THT]"]
  R1 = Resistor [tolerance=±5% resistance=330 package=THT]

nets:
  N1: Raspberry_Pi1.GPIO24, LED1.anode
  N2: Raspberry_Pi1.GPIO23, S1.Pin_1, S1.Pin_2
  N3: Raspberry_Pi1.GND, S1.Pin_3, S1.Pin_4, R1.Pin_1
  N4: LED1.cathode, R1.Pin_0
