# Fritzing sketch LED GPIO (saved by Fritzing 0.9.3b)
breadboards: 1

parts:
  Raspberry_Pi_A1 = Raspberry Pi A
  R1 = Resistor [tolerance=±5% resistance=330 package=THT]
  LED2 = LED - 5mm [color="Red (633nm)" package="5 mm [THT]"]

nets:
  N1: Raspberry_Pi_A1.GND, R1.Pin_0
  N2: Raspberry_Pi_A1.GPIO_18, LED2.anode
  N3: R1.Pin_1, LED2.cathode
