# Fritzing sketch LED Switch (saved by Fritzing 0.9.3b)
breadboards: 1

parts:
  S1 = Pushbutton [package="[THT]"]
  R1 = Resistor [tolerance=±5% resistance=10k package=THT]
  Raspberry_Pi_A1 = Raspberry Pi A
  R2 = Resistor [tolerance=±5% resistance=270 package=THT]
  LED1 = LED - 5mm [color="White (4500K)" package="5 mm [THT]"]

nets:
  N1: S1.Pin_1, S1.Pin_2, R1.Pin_0
  N2: S1.Pin_3, S1.Pin_4, Raspberry_Pi_A1.3V3
  N3: R1.Pin_1, Raspberry_Pi_A1.GND, R2.Pin_1
  N4: Raspberry_Pi_A1.GPIO_24, LED1.cathode
  N5: R2.Pin_0, LED1.anode
