# Fritzing sketch BH1750 (saved by Fritzing 0.9.4)
breadboards: 1

parts:
  Raspberry_Pi_1 = Raspberry Pi 3 [part_number=RPI-3-V1.2]
  JP1 = Header 6 [package=1x06-smd-female-v2]

nets:
  N1: Raspberry_Pi_1.3v3, JP1.1
  N2: Raspberry_Pi_1.GPIO2, JP1.4
  N3: Raspberry_Pi_1.GPIO3, JP1.3
  N4: Raspberry_Pi_1.GND, JP1.2

notes:
  Vcc
  GND
  SCL
  SDA
  ADDR
  BH1750
