# Fritzing sketch LED (saved by Fritzing 0.9.4)
breadboards: 1

parts:
  LED1 = LED - 5mm [color="Red (633nm)" package="5 mm [THT]"]
  Raspberry_Pi_1 = Raspberry Pi 3 [part_number=RPI-3-V1.2]
  R2 = Resistor [tolerance=±5% resistance=220 package=THT]

nets:
  N1: LED1.cathode, R2.Pin_0
  N2: LED1.anode, Raspberry_Pi_1.GPIO18
  N3: Raspberry_Pi_1.GND, R2.Pin_1
