# Fritzing sketch JoystickLedTest (saved by Fritzing 0.9.3b)
breadboards: 1

parts:
  C_H_I_P_1 = Next Thing Co. C.H.I.P
  IC1 = Microchip PCF8591 4 Channel AD/DA expander [part_number=PCF8591 package="DIP (Dual Inline) [THT]"]
  Part1 = Thumb Joystick
  R1 = Resistor [tolerance=±5% resistance=220 package="1206 [SMD]"]
  R2 = Resistor [tolerance=±5% resistance=220 package="1206 [SMD]"]
  LED2 = smd LED [color="Red (633nm)" package="0603 [SMD]"]
  LED3 = smd LED [color="Red (633nm)" package="0603 [SMD]"]
  IC2 = Microchip PCF8591 4 Channel AD/DA expander [part_number=PCF8591 package="DIP (Dual Inline) [THT]"]

nets:
  GND: C_H_I_P_1.GND, IC1.A0, IC1.A1, IC1.A2, IC1.VSS, IC1.EXT, IC1.AGND, Part1.GND, R1.Pin_1, R2.Pin_1, IC2.A0, IC2.A1, IC2.A2, IC2.VSS, IC2.EXT, IC2.AGND
  N1: C_H_I_P_1.TWI1-SDA, IC1.SDA, IC2.SDA
  N2: C_H_I_P_1.TWI1-SCK, IC1.SCL, IC2.SCL
  N3: C_H_I_P_1.PWM0, LED3.anode
  VDD: C_H_I_P_1.VCC-3V3, IC1.VDD, Part1.VCC, IC2.VDD
  N4: C_H_I_P_1.CSID6, LED2.anode
  N5: IC1.AIN0, Part1.SEL, Part1.HORZ, IC2.AIN0
  N6: IC1.AIN1, Part1.VERT, IC2.AIN1
  N7: IC1.AIN2, IC2.AIN2
  N8: IC1.AIN3, IC2.AIN3
  N9: IC1.OSC, IC2.OSC
  N10: IC1.VREF, IC2.VREF
  N11: IC1.AOUT, IC2.AOUT
  N12: R1.Pin_0, LED2.cathode
  N13: R2.Pin_0, LED3.cathode
