# Fritzing sketch MCP23017_LED_Button (saved by Fritzing 0.9.2b)
breadboards: 1

parts:
  IC1 = MCP23017 I2C I/O Expander
  Raspberry_Pi1 = Raspberry Pi 2
  LED1 = smd LED [color="Red (633nm)" package="0603 [SMD]"]
  R1 = Resistor [tolerance=±5% resistance=220 package="1206 [SMD]"]
  S1 = Momentary Switch [package=ksa_sealed_tac_switch]

nets:
  N1: IC1.GPB0, S1.2
  VDD: IC1.VDD, IC1.RESET, Raspberry_Pi1.3v3
  VSS: IC1.VSS, IC1.A0, IC1.A1, IC1.A2, Raspberry_Pi1.GND, R1.Pin_0, S1.4
  N2: IC1.SCL, Raspberry_Pi1.GPIO3, Raspberry_Pi1.GPIO4
  N3: IC1.SDA, Raspberry_Pi1.GPIO2
  N4: IC1.INTB, Raspberry_Pi1.GPIO24
  N5: IC1.INTA, Raspberry_Pi1.GPIO23
  N6: IC1.GPA7, LED1.anode
  N7: LED1.cathode, R1.Pin_1

custom parts:
  MCP23017 I2C I/O Expander: MCP23017 I2C 16-Channel I/O Expander
