# Fritzing sketch MCP3008_LDR (saved by Fritzing 0.9.3b)
breadboards: 1

parts:
  IC1 = MCP3008 8-channel 10-bit ADC [part_number=MCP3008]
  RaspberryPi1 = Raspberry Pi Model B
  R2 = Resistor [tolerance=±5% resistance=220 package=THT]
  R3 = Photocell (LDR) [package=THT]

nets:
  N1: IC1.no_name_yet#1, R2.Pin_1, R3.pin_1
  N2: IC1.no_name_yet#9, IC1.no_name_yet#14, RaspberryPi1.GND, R3.pin_0
  N3: IC1.no_name_yet#10, RaspberryPi1.CS1
  N4: IC1.no_name_yet#11, RaspberryPi1.MOSI
  N5: IC1.no_name_yet#12, RaspberryPi1.MISO, RaspberryPi1.#25
  N6: IC1.no_name_yet#13, RaspberryPi1.SCLK
  N7: IC1.no_name_yet#15, IC1.no_name_yet#16, RaspberryPi1.5V, R2.Pin_0

custom parts:
  Raspberry Pi Model B: Raspberry Pi (Model B)
